# Fritzing sketch Untitled Sketch 4 (saved by Fritzing 0.9.3b)
breadboards: 1

parts:
  Sensor1 = Gas Sensor Breakout Board
  U1 = ESP8266 NodeMCU LoLin module
  DHT1 = Humidity and Temperature Sensor DHT11
  R1 = Resistor [tolerance=±5% resistance=1k package="0402 [SMD]"]
  Grove1 = Grove OLED 128x96
  SG1 = Buzzer 12mm [package=buzzer-ccv]
  LED1 = LED - 5mm [color="Red (633nm)" package="5 mm [THT]"]

nets:
  GND: Sensor1.GND, U1.GND, Grove1.GND, SG1.1, LED1.cathode
  N1: Sensor1.AOUT, U1.A0
  VCC: Sensor1.5V, U1.3V3, DHT1.Vcc, R1.Pin_1, Grove1.VCC, SG1.2
  N2: U1.D1, Grove1.SCL
  N3: U1.D2, Grove1.SDA
  N4: U1.D4, DHT1.Data-signal, R1.Pin_0
  N5: U1.D6, LED1.anode

custom parts:
  Gas Sensor Breakout Board: Gas sensor breakout board. Input voltage is 5V. Sensor output is available in analog and digital.
  ESP8266 NodeMCU LoLin module: ESP8266 based NodeMCU
  Humidity and Temperature Sensor DHT11: Digital relative humidity & temperature sensor DHT11
