# Fritzing sketch Untitled Sketch2 4 (saved by Fritzing 0.9.3b)
breadboards: 1

parts:
  Sensor1 = Gas Sensor Breakout Board
  DHT1 = Humidity and Temperature Sensor DHT11
  Grove1 = Grove OLED 128x96
  LED1 = LED - 5mm [color="Red (633nm)" package="5 mm [THT]"]
  R2 = Resistor [tolerance=±5% resistance=1k package=THT]
  U1 = ESP8266 NodeMCU LoLin base
  buz1 = Piezo Buzzer
  R3 = Resistor [tolerance=±5% resistance=1k package="2512 [SMD]"]

nets:
  GND: Sensor1.GND, DHT1.GND_1, Grove1.GND, U1.GND2-0, U1.GND2-1, U1.GND3-2, U1.GND8-4, U1.GND8-5, U1.GND8-7, buz1.pin_2
  N1: Sensor1.AOUT, U1.A0
  5V: Sensor1.5V, Grove1.VCC, U1.VIN, U1.5V-0, U1.5V-3
  N2: DHT1.Vcc, R3.Pin_1
  N3: DHT1.Data-signal, R3.Pin_0
  N4: Grove1.SDA, U1.D2-0, U1.D2-3
  N5: Grove1.SCL, U1.D1-0, U1.D1-3
  N6: LED1.anode, R2.Pin_0
  N7: R2.Pin_1, U1.D6-0, U1.D6-3
  N8: U1.D5-0, U1.D5-2, buz1.pin_1

custom parts:
  Gas Sensor Breakout Board: Gas sensor breakout board. Input voltage is 5V. Sensor output is available in analog and digital.
  Humidity and Temperature Sensor DHT11: Digital relative humidity & temperature sensor DHT11
  ESP8266 NodeMCU LoLin base: ESP8266 based NodeMCU Base
  Piezo Buzzer: Part from https://www.nutsvolts.com/magazine/article/november2012_SmileysWorkshop modified to be .3 in spacing to match the adafruit buzzer 5V breadboard friendly part.
